# Fritzing sketch Feather Flex sensor and RGB LED (saved by Fritzing 0.8.7b)
breadboards: 1

parts:
  Part2 = Adafruit Feather 32u4 Bluefruit [part_number="Adafruit #2829"]
  RGB_LED = RGB LED (com. cathode, rgb) [package="5 mm [THT]"]
  R3 = Resistor [tolerance=±5% resistance=220 package=THT]
  R1 = Resistor [tolerance=±5% resistance=220 package=THT]
  R2 = Resistor [tolerance=±5% resistance=220 package=THT]
  R5 = Resistor [tolerance=±5% resistance=47k package=THT]
  R4 = Basic Flex Resistor

nets:
  N1: Part2.A0, R5.Pin_1, R4.pin_1
  N2: Part2.GND, RGB_LED.common_cathode, R5.Pin_0
  N3: Part2.+3V3, R4.Pin_2
  N4: Part2.11, R2.Pin_1
  N5: Part2.9, R1.Pin_1
  N6: Part2.5, R3.Pin_1
  N7: RGB_LED.red_anode, R3.Pin_0
  N8: RGB_LED.green_anode, R1.Pin_0
  N9: RGB_LED.blue_anode, R2.Pin_0

notes:
  OUTPUT:
  RBG LED
  Resistor - 220 Ohms
  INPUT:
  Flex sensor
  Resistor - 10K Ohms

custom parts:
  Adafruit Feather 32u4 Bluefruit: This is the Adafruit Feather 32u4 Bluefruit - our take on an 'all-in-one' Arduino-compatible + Bluetooth Low Energy with built in USB and battery charging. Its an Adafruit Feather 32u4 with a BTLE module, ready to rock! We have other boards in the Feather family, check'em out here. Bluetooth Low Energy is the hottest new low-power, 2.4GHz spectrum wireless protocol. In particular, its the only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
