# Fritzing sketch Feather Temperature and Buzzer (saved by Fritzing 0.8.7b)
breadboards: 1

parts:
  Part5 = Adafruit Feather 32u4 Bluefruit [part_number="Adafruit #2829"]
  Temperature_Sensor = TMP36 [package=to-92-kit]
  Piezo_Buzzer = Piezo Speaker

nets:
  N1: Part5.A0, Temperature_Sensor.VOUT
  GND: Part5.GND, Temperature_Sensor.GND, Piezo_Buzzer.pin1
  +3V3: Part5.+3V3, Temperature_Sensor.VCC
  N2: Part5.9, Piezo_Buzzer.pin2

notes:
  OUTPUT:
  Piezo buzzer
  INPUT:
  Temperature
  Check Polarity!

custom parts:
  Adafruit Feather 32u4 Bluefruit: This is the Adafruit Feather 32u4 Bluefruit - our take on an 'all-in-one' Arduino-compatible + Bluetooth Low Energy with built in USB and battery charging. Its an Adafruit Feather 32u4 with a BTLE module, ready to rock! We have other boards in the Feather family, check'em out here. Bluetooth Low Energy is the hottest new low-power, 2.4GHz spectrum wireless protocol. In particular, its the only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
