# Fritzing sketch Feather Tilt Switch and 2 LEDs (saved by Fritzing 0.8.7b)
breadboards: 1

parts:
  Tilt_Switch = Tilt Switch [package=THT]
  Part3 = Adafruit Feather 32u4 Bluefruit [part_number="Adafruit #2829"]
  R1 = Resistor [tolerance=±5% resistance=220 package=THT]
  LED1 = LED - 3mm [color="Red (633nm)" package="3 mm [THT]"]
  LED2 = LED - 3mm [color="Green (565nm)" package="3 mm [THT]"]
  R2 = Resistor [tolerance=±5% resistance=220 package=THT]

nets:
  N1: Tilt_Switch.Pin_1, Part3.GND, R1.Pin_1, R2.Pin_1
  N2: Tilt_Switch.Pin_2, Part3.12
  N3: Part3.11, LED2.anode
  N4: Part3.9, LED1.anode
  N5: R1.Pin_0, LED2.cathode
  N6: LED1.cathode, R2.Pin_0

notes:
  INPUT:
  tilt switch
  OUTPUT:
  Multiple LEDs
  Resistor - 220 Ohms

custom parts:
  Adafruit Feather 32u4 Bluefruit: This is the Adafruit Feather 32u4 Bluefruit - our take on an 'all-in-one' Arduino-compatible + Bluetooth Low Energy with built in USB and battery charging. Its an Adafruit Feather 32u4 with a BTLE module, ready to rock! We have other boards in the Feather family, check'em out here. Bluetooth Low Energy is the hottest new low-power, 2.4GHz spectrum wireless protocol. In particular, its the only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
