# Fritzing sketch Ultrasonic Proximity Sensor and Servo (saved by Fritzing 0.8.7b)
breadboards: 1

parts:
  Part6 = Arduino Uno (Rev3)
  Servo = Basic Servo
  Ultrasonic_Proximity_Sensor = SRF05 Ultrasonic Rangefinder

nets:
  N1: Part6.D10_PWM/SS, Ultrasonic_Proximity_Sensor.Trig
  N2: Part6.D11_PWM/MOSI, Ultrasonic_Proximity_Sensor.Echo
  N3: Part6.D12/MISO, Servo.pulse
  VCC: Part6.5V, Servo.vcc, Ultrasonic_Proximity_Sensor.VCC
  GND: Part6.GND, Servo.gnd, Ultrasonic_Proximity_Sensor.GND

notes:
  OUTPUT:
  Servo motor
  Requires 5V
  INPUT:
  Ultrasonic Range Finder
  Requires 5V
