# Fritzing sketch Ultrasonic Proximity Sensor with NeoPixel Stick (saved by Fritzing 0.8.7b)
breadboards: 1

parts:
  Part1 = Arduino Uno (Rev3)
  Part2 = SRF05 Ultrasonic Rangefinder
  Part3 = NeoPixel Stick [part_number=1426]

nets:
  N1: Part1.D9_PWM, Part2.Echo
  N2: Part1.D10_PWM/SS, Part2.Trig
  GND: Part1.GND, Part2.GND, Part3.GND
  N3: Part1.D6_PWM, Part3.DATAIN
  5V: Part1.5V, Part2.VCC, Part3.+5V

custom parts:
  NeoPixel Stick: Make your own little LED strip arrangement with this stick of NeoPixel LEDs. We crammed 8 of the tiny 5050 (5mm x 5mm) smart RGB LEDs onto a PCB with mounting holes and a chainable design. Use only one microcontroller pin to control as many as you can chain together! Each LED is addressable as the driver chip is inside the LED. Each one has ~18mA constant current drive so the color will be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
