# Fritzing sketch analogTempSensorAndRGBLED (saved by Fritzing 0.8.7b)
breadboards: 1

parts:
  Part1 = Arduino Uno (Rev3)
  R1 = Resistor [tolerance=±5% resistance=220 package=THT]
  R2 = Resistor [tolerance=±5% resistance=220 package=THT]
  R3 = Resistor [tolerance=±5% resistance=220 package=THT]
  LED2 = RGB LED (com. cathode, rbg) [package="5 mm [THT]"]
  U1 = TMP36 [package=to-92]

nets:
  N1: Part1.A0, U1.VOUT
  N2: Part1.D9_PWM, R3.Pin_0
  N3: Part1.D10_PWM/SS, R2.Pin_0
  N4: Part1.D11_PWM/MOSI, R1.Pin_0
  5V: Part1.5V, U1.VCC
  GND: Part1.GND, LED2.common_cathode, U1.GND
  N5: R1.Pin_1, LED2.red_anode
  N6: R2.Pin_1, LED2.blue_anode
  N7: R3.Pin_1, LED2.green_anode
